// Logisim project part1_2.circ as structural Verilog: 7 circuits, main circuit main
module main (
  input  in_1,
  input  in_2,
  input  in_3,
  input  in_4,
  input  in_5,
  input  in_6,
  input  in_7,
  input  in_8,
  input  in_9,
  input  in_10,
  input  in_11,
  input  in_12,
  input  in_13,
  input  in_14,
  input  in_15,
  output out_16,
  output out_17,
  output out_18,
  output out_19,
  output out_20,
  output [7:0] val_of_adder,
  output [7:0] val_of_reg
);

  MY_XOR my_xor_1 (.in_1(in_1), .in_2(in_2), .out_3(out_16));
  MY_NAND my_nand_1 (.in_1(in_5), .in_2(in_7), .out_3(out_18));
  MY_NOR my_nor_1 (.in_1(in_11), .in_2(in_12), .out_3(out_19));
  MY_21MUX my_21mux_1 (.A(in_13), .B(in_14), .S(in_15), .out_4(out_20));
  AddMachine addmachine_1 (.out_1(val_of_adder), .out_2(val_of_reg));
  MY_41MUX my_41mux_1 (.A(in_3), .B(in_4), .C(in_6), .D(in_8), .S1(in_9), .S2(in_10), .out_7(out_17));
endmodule

module MY_NAND (
  input  in_1,
  input  in_2,
  output out_3
);

  wire and_1_out;

  and and_1 (and_1_out, in_1, in_2);
  not not_1 (out_3, and_1_out);
endmodule

module MY_XOR (
  input  in_1,
  input  in_2,
  output out_3
);

  wire and_1_out, and_2_out, not_1_out, not_2_out;

  not not_1 (not_1_out, in_1);
  and and_1 (and_1_out, not_1_out, in_2);
  not not_2 (not_2_out, in_2);
  and and_2 (and_2_out, in_1, not_2_out);
  or or_1 (out_3, and_2_out, and_1_out);
endmodule

module MY_NOR (
  input  in_1,
  input  in_2,
  output out_3
);

  wire or_1_out;

  or or_1 (or_1_out, in_1, in_2);
  not not_1 (out_3, or_1_out);
endmodule

module MY_21MUX (
  input  A,
  input  B,
  input  S,
  output out_4
);

  wire and_1_out, and_2_out, not_1_out;

  and and_1 (and_1_out, B, S);
  and and_2 (and_2_out, A, not_1_out);
  not not_1 (not_1_out, S);
  or or_1 (out_4, and_2_out, and_1_out);
endmodule

module MY_41MUX (
  input  A,
  input  B,
  input  C,
  input  D,
  input  S1,
  input  S2,
  output out_7
);

  wire my_21mux_1_out_4, my_21mux_2_out_4;

  MY_21MUX my_21mux_1 (.A(A), .B(B), .S(S1), .out_4(my_21mux_1_out_4));
  MY_21MUX my_21mux_2 (.A(C), .B(D), .S(S1), .out_4(my_21mux_2_out_4));
  MY_21MUX my_21mux_3 (.A(my_21mux_1_out_4), .B(my_21mux_2_out_4), .S(S2), .out_4(out_7));
endmodule

module AddMachine (
  output [7:0] out_1,
  output [7:0] out_2
);

  wire clock_1_out;

  Adder adder_1 (.a(8'h1), .b(out_2), .out(out_1));  // open: cin, cout
  Register register_1 (.D(out_1), .clk(clock_1_out), .Q(out_2));  // open: en, clr
  Clock clock_1 (.out(clock_1_out));
endmodule
