// Logisim project fibonacci.circ as structural Verilog: 2 circuits, main circuit main
module main (
  output [15:0] out_1
);

  wire clock_1_out, comparator_1_eq, not_1_out;
  wire [15:0] adder_1_out, register_1_q;

  // Probe on adder_1_out
  Adder #(.width(16)) adder_1 (.a(16'h1), .b(register_1_q), .out(adder_1_out));  // open: cin, cout
  Register #(.width(16)) register_1 (
    .D(adder_1_out), .en(not_1_out), .clk(clock_1_out), .Q(register_1_q));  // open: clr
  Clock clock_1 (.out(clock_1_out));
  // Probe on comparator_1_eq
  Comparator #(.width(16)) comparator_1 (.a(adder_1_out), .b(16'hf), .eq(comparator_1_eq));  // open: gt, lt
  not not_1 (not_1_out, comparator_1_eq);
  FibAdder fibadder_1 (.Count(adder_1_out), .StopAdder(not_1_out), .out_3(out_1));
endmodule

module FibAdder (
  input  [15:0] Count,
  input  StopAdder,
  output [15:0] out_3
);

  wire clock_1_out, clock_2_out, comparator_1_eq;
  wire [15:0] multiplexer_1_out, register_1_q, register_2_q;

  Comparator #(.width(16)) comparator_1 (.a(Count), .b(16'h1), .eq(comparator_1_eq));  // open: gt, lt
  Multiplexer #(.width(16), .enable("false")) multiplexer_1 (
    .in0(out_3), .in1(16'h1), .out(multiplexer_1_out), .sel(comparator_1_eq));
  Register #(.width(16)) register_1 (
    .D(multiplexer_1_out), .en(StopAdder), .clk(clock_1_out), .Q(register_1_q));  // open: clr
  Clock clock_1 (.out(clock_1_out));
  Register #(.width(16)) register_2 (
    .D(register_1_q), .en(StopAdder), .clk(clock_2_out), .Q(register_2_q));  // open: clr
  Clock clock_2 (.out(clock_2_out));
  Adder #(.width(16)) adder_1 (.a(register_1_q), .b(register_2_q), .out(out_3));  // open: cin, cout

  // Notes on the sheet:
  //   Fn-1
  //   Fn-2
endmodule
